// Digital circuit part_c.dig as structural Verilog
module part_c (
  input  in_0,
  input  in_2,
  input  in_1,
  output out_0
);

  wire fgnfet_3_s, fgnfet_5_s, fgnfet_7_s, fgnfet_9_s, fgnfet_11_s, fgpfet_1_d, fgpfet_2_d, fgpfet_3_s,
       fgpfet_4_s, fgpfet_7_s, fgpfet_8_d, fgpfet_11_s, fgpfet_13_d;

  FGPFET fgpfet_1 (.G(in_0), .S(1'b1), .D(fgpfet_1_d));
  FGNFET fgnfet_1 (.G(in_0), .D(fgpfet_1_d), .S(1'b0));
  FGPFET fgpfet_2 (.G(in_1), .S(1'b1), .D(fgpfet_2_d));
  FGNFET fgnfet_2 (.G(in_1), .D(fgpfet_2_d), .S(1'b0));
  FGPFET fgpfet_3 (.G(fgpfet_2_d), .S(fgpfet_3_s), .D(1'b0));
  FGPFET fgpfet_4 (.G(in_1), .S(fgpfet_4_s), .D(1'b0));
  FGPFET fgpfet_5 (.G(in_0), .S(fgpfet_3_s), .D(1'b0));
  FGNFET fgnfet_3 (.G(fgpfet_1_d), .D(1'b1), .S(fgnfet_3_s));
  FGNFET fgnfet_4 (.G(in_1), .D(fgnfet_3_s), .S(fgpfet_4_s));
  FGPFET fgpfet_6 (.G(fgpfet_1_d), .S(fgpfet_4_s), .D(1'b0));
  FGNFET fgnfet_5 (.G(in_0), .D(1'b1), .S(fgnfet_5_s));
  FGNFET fgnfet_6 (.G(fgpfet_2_d), .D(fgnfet_5_s), .S(fgpfet_3_s));
  FGNFET fgnfet_7 (.G(fgpfet_4_s), .D(1'b1), .S(fgnfet_7_s));
  FGPFET fgpfet_7 (.G(in_1), .S(fgpfet_7_s), .D(1'b0));
  FGNFET fgnfet_8 (.G(fgpfet_3_s), .D(1'b1), .S(fgnfet_7_s));
  FGPFET fgpfet_8 (.G(fgpfet_3_s), .S(fgnfet_7_s), .D(fgpfet_8_d));
  FGPFET fgpfet_9 (.G(fgpfet_4_s), .S(fgpfet_8_d), .D(1'b0));
  FGNFET fgnfet_9 (.G(in_0), .D(1'b1), .S(fgnfet_9_s));
  FGNFET fgnfet_10 (.G(in_1), .D(fgnfet_9_s), .S(fgpfet_7_s));
  FGPFET fgpfet_10 (.G(in_0), .S(fgpfet_7_s), .D(1'b0));
  FGPFET fgpfet_11 (.G(in_2), .S(fgpfet_11_s), .D(1'b0));
  FGNFET fgnfet_11 (.G(fgnfet_7_s), .D(1'b1), .S(fgnfet_11_s));
  FGNFET fgnfet_12 (.G(in_2), .D(fgnfet_11_s), .S(fgpfet_11_s));
  FGPFET fgpfet_12 (.G(fgnfet_7_s), .S(fgpfet_11_s), .D(1'b0));
  FGNFET fgnfet_13 (.G(fgpfet_7_s), .D(1'b1), .S(out_0));
  FGPFET fgpfet_13 (.G(fgpfet_11_s), .S(out_0), .D(fgpfet_13_d));
  FGPFET fgpfet_14 (.G(fgpfet_7_s), .S(fgpfet_13_d), .D(1'b0));
  FGNFET fgnfet_14 (.G(fgpfet_11_s), .D(1'b1), .S(out_0));
endmodule

/* Test case:
in_0 in_1 in_2 out_0
0 0 0 0
0 0 1 0
0 1 0 0
0 1 1 1
1 0 0 0
1 0 1 1
1 1 0 1
1 1 1 1
*/
