// Digital circuit lab2_part2.dig as structural Verilog
module lab2_part2 (
  input  in0,
  input  in1,
  input  in2,
  input  in3,
  output sign_a,
  output sign_f,
  output sign_b,
  output sign_g,
  output sign_e,
  output sign_c,
  output sign_d,
  output sign_dp,
  output seg_a,
  output seg_f,
  output seg_b,
  output seg_g,
  output seg_e,
  output seg_c,
  output seg_d,
  output seg_dp
);

  wire and_1_out, and_2_out, and_3_out, and_4_out, and_5_out, and_6_out, and_7_out, and_8_out, not_1_out,
       not_2_out, not_3_out, not_4_out, not_5_out, not_6_out, not_7_out, not_8_out, not_9_out, not_10_out,
       not_11_out, not_12_out, not_13_out, not_14_out, not_15_out, or_1_out, or_2_out, or_3_out, or_4_out,
       or_5_out, or_6_out, or_7_out, or_8_out, or_9_out, or_10_out, or_11_out;

  Seven_Seg seven_seg_1 (.a(1'b0), .b(1'b0), .c(1'b0), .d(1'b0), .e(1'b0), .f(1'b0), .g(in3), .dp(1'b0));
  Seven_Seg seven_seg_2 (.a(seg_a), .b(seg_b), .c(seg_c), .d(seg_d), .e(seg_e), .f(seg_f), .g(seg_g), .dp(1'b0));
  not not_1 (not_1_out, in1);
  not not_2 (not_2_out, in0);
  or or_1 (or_1_out, in0, in1);
  and and_1 (and_1_out, not_3_out, in1);
  not not_3 (not_3_out, in0);
  and and_2 (and_2_out, in0, not_1_out);
  or or_2 (or_2_out, not_2_out, in1);
  or or_3 (or_3_out, and_1_out, and_2_out);
  Multiplexer #(.Selector_Bits(2)) multiplexer_1 (
    .sel({in3, in2}), .in_0(or_2_out), .in_1(or_1_out), .in_2(1'b1), .in_3(or_3_out), .out(seg_a));
  not not_4 (not_4_out, in0);
  not not_5 (not_5_out, in1);
  not not_6 (not_6_out, in1);
  and and_3 (and_3_out, not_4_out, not_5_out);
  and and_4 (and_4_out, in0, in1);
  or or_4 (or_4_out, and_3_out, and_4_out);
  Multiplexer #(.Selector_Bits(2)) multiplexer_2 (
    .sel({in3, in2}), .in_0(1'b1), .in_1(or_4_out), .in_2(not_6_out), .in_3(1'b1), .out(seg_b));
  not not_7 (not_7_out, in1);
  or or_5 (or_5_out, in0, not_7_out);
  Multiplexer #(.Selector_Bits(2)) multiplexer_3 (
    .sel({in3, in2}), .in_0(or_5_out), .in_1(1'b1), .in_2(1'b1), .in_3(or_5_out), .out(seg_c));
  not not_8 (not_8_out, in0);
  not not_9 (not_9_out, in0);
  not not_10 (not_10_out, in1);
  or or_6 (or_6_out, not_8_out, in1);
  and and_5 (and_5_out, not_9_out, in1);
  and and_6 (and_6_out, in0, not_10_out);
  or or_7 (or_7_out, and_5_out, and_6_out);
  Multiplexer #(.Selector_Bits(2)) multiplexer_4 (
    .sel({in3, in2}), .in_0(or_6_out), .in_1(or_7_out), .in_2(or_6_out), .in_3(or_7_out), .out(seg_d));
  not not_11 (not_11_out, in0);
  and and_7 (and_7_out, not_11_out, in1);
  Multiplexer #(.Selector_Bits(2)) multiplexer_5 (
    .sel({in3, in2}), .in_0(not_11_out), .in_1(and_7_out), .in_2(not_11_out), .in_3(and_7_out), .out(seg_e));
  not not_12 (not_12_out, in1);
  not not_13 (not_13_out, in0);
  and and_8 (and_8_out, not_13_out, not_12_out);
  or or_8 (or_8_out, not_13_out, not_12_out);
  or or_9 (or_9_out, not_13_out, in1);
  Multiplexer #(.Selector_Bits(2)) multiplexer_6 (
    .sel({in3, in2}), .in_0(and_8_out), .in_1(or_8_out), .in_2(or_9_out), .in_3(and_8_out), .out(seg_f));
  not not_14 (not_14_out, in0);
  not not_15 (not_15_out, in1);
  or or_10 (or_10_out, in1, not_14_out);
  or or_11 (or_11_out, not_14_out, not_15_out);
  Multiplexer #(.Selector_Bits(2)) multiplexer_7 (
    .sel({in3, in2}), .in_0(in1), .in_1(or_11_out), .in_2(or_10_out), .in_3(or_11_out), .out(seg_g));

  assign seg_dp = 1'b0;
  assign sign_a = 1'b0;
  assign sign_b = 1'b0;
  assign sign_c = 1'b0;
  assign sign_d = 1'b0;
  assign sign_dp = 1'b0;
  assign sign_e = 1'b0;
  assign sign_f = 1'b0;
  assign sign_g = in3;

  // Notes on the sheet:
  //   Interface (do not edit the content inside this box)
  //   Outputs:
  //   Inputs
  //   Sign
  //   Decimal Number
  //   B
  //   A
endmodule

/* Test case:
in3 in2 in1 in0  sign_a sign_b sign_c sign_d sign_e sign_f sign_g  seg_a seg_b seg_c seg_d seg_e seg_f seg_g
 0   0   0   0    0      0      0      0      0      0      0       1     1     1     1     1     1     0
*/
